# Fritzing sketch Connect Wires Breadboard Schematic (saved by Fritzing 0.9.10b)
breadboards: 1

parts:
  Part1 = Arduino Nano (Rev3.0)
  Status_LED = Adafruit Breadboard-Friendly NeoPixel [part_number="Adafruit #1312"]
  Command_and_Power = JST-03JQ-BT [part_number=JST-JQ-BT package=THT]
  Driver = Camdenboss CTB0158-4 [part_number=CTB0158-4 package=THT]
  Receive = Camdenboss CTB0158-4 [part_number=CTB0158-4 package=THT]
  BULB_Bit_4 = Incandescent light bulb small [package="bulb sm"]
  BULB_Bit_3 = Incandescent light bulb small [package="bulb sm"]
  BULB_Bit_2 = Incandescent light bulb small [package="bulb sm"]
  BULB_Bit_1 = Incandescent light bulb small [package="bulb sm"]
  CLIP3 = Alligator Clip
  CLIP7 = Alligator Clip
  CLIP6 = Alligator Clip
  CLIP8 = Alligator Clip
  CLIP5 = Alligator Clip
  CLIP1 = Alligator Clip
  CLIP4 = Alligator Clip
  CLIP2 = Alligator Clip

nets:
  GND: Part1.GND, Status_LED.GND, Command_and_Power.pin3, BULB_Bit_4.1, BULB_Bit_3.1, BULB_Bit_2.1, BULB_Bit_1.1
  N1: Part1.D2, Driver.pin4
  N2: Part1.D3, Driver.pin3
  N3: Part1.D4, Driver.pin2
  N4: Part1.D5, Driver.pin1
  N5: Part1.D6, Receive.pin1
  N6: Part1.D7, Receive.pin2
  N7: Part1.D8, Receive.pin3
  N8: Part1.D9, Receive.pin4
  VIN: Part1.VIN, Status_LED.VDD, Command_and_Power.pin2
  N9: Part1.A5, BULB_Bit_4.2
  N10: Part1.A4, BULB_Bit_3.2
  N11: Part1.A3, BULB_Bit_2.2
  N12: Part1.A2, BULB_Bit_1.2
  N13: Part1.A1, Command_and_Power.pin1
  N14: Part1.A0, Status_LED.IN
  N15: CLIP3.wire, CLIP4.wire
  N16: CLIP7.wire, CLIP8.wire
  N17: CLIP6.wire, CLIP5.wire
  N18: CLIP1.wire, CLIP2.wire

custom parts:
  Adafruit Breadboard-Friendly NeoPixel: This is the easiest way possible to add small, bright RGB pixels to your project. We took the same technology from our Flora NeoPixels and made them breadboard friendly, with two rows of 3 x 0.1" spaced header on each side for easy soldering, chaining and breadboarding. These ultra-bright LEDs have a constant-current driver cooked right into the LED package! The pixels are chainable - so you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
  Alligator Clip: Alligator clip
  Alligator Clip: Alligator clip
  Alligator Clip: Alligator clip
  Alligator Clip: Alligator clip
