# Fritzing sketch Dialer Breadboard Schematic (saved by Fritzing 0.9.10b)
breadboards: 1

parts:
  Part1 = Arduino Nano (Rev3.0)
  Part2 = Adafruit Breadboard-Friendly NeoPixel [part_number="Adafruit #1312"]
  DFRobot_DFPlayer_Mini1 = DFRobot DFPlayer Mini [part_number=DFR0299]
  Online = Pushbutton [package=THT]
  Phone_Pulse = Pushbutton [package=THT]
  Phone_Dialing = Pushbutton [package=THT]
  SP1 = SPEAKER [package=pcb_mount_speaker]
  R1 = Resistor [tolerance=±5% power=0.25 resistance=1100 package=THT]
  R2 = Resistor [tolerance=±5% power=0.25 resistance=2200 package=THT]
  Command_and_Power = JST-03JQ-BT [part_number=JST-JQ-BT package=THT]

nets (from the schematic view):
  GND: Part1.GND, Part2.GND, DFRobot_DFPlayer_Mini1.GND-1, DFRobot_DFPlayer_Mini1.GND-2, Online.leg1, Phone_Pulse.leg1, Phone_Dialing.leg1, R2.Pin_0, Command_and_Power.pin3
  N1: Part1.D2, Online.leg0
  N2: Part1.D3, Phone_Dialing.leg0
  N3: Part1.D4, Phone_Pulse.leg0
  N4: Part1.D11/MOSI, DFRobot_DFPlayer_Mini1.TX
  N5: Part1.D12/MISO, R1.Pin_0
  VIN: Part1.VIN, Part2.VDD, DFRobot_DFPlayer_Mini1.VCC, Command_and_Power.pin2
  N6: Part1.A1, Command_and_Power.pin1
  N7: Part1.A0, Part2.IN
  N8: DFRobot_DFPlayer_Mini1.RX, R1.Pin_1, R2.Pin_1
  N9: DFRobot_DFPlayer_Mini1.SPK_1, SP1.-
  N10: DFRobot_DFPlayer_Mini1.SPK_2, SP1.+

custom parts:
  Adafruit Breadboard-Friendly NeoPixel: This is the easiest way possible to add small, bright RGB pixels to your project. We took the same technology from our Flora NeoPixels and made them breadboard friendly, with two rows of 3 x 0.1" spaced header on each side for easy soldering, chaining and breadboarding. These ultra-bright LEDs have a constant-current driver cooked right into the LED package! The pixels are chainable - so you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
