# Fritzing sketch Slider Breadboard Schematic (saved by Fritzing 0.9.10b)
breadboards: 1

parts:
  Part1 = Arduino Nano (Rev3.0)
  Slider_1 = Slide Potentiometer [maximum_resistance=10kΩ knob_status=50% power=0.5W]
  Slider_2 = Slide Potentiometer [maximum_resistance=10kΩ knob_status=50% power=0.5W]
  Slider_3 = Slide Potentiometer [maximum_resistance=10kΩ knob_status=50% power=0.5W]
  Part3 = Adafruit Breadboard-Friendly NeoPixel [part_number="Adafruit #1312"]
  Slider_1_Green_LED = smd LED [color="Green (560nm)" package="0603 [SMD]"]
  Slider_2_Red_LED = smd LED [color="Red (633nm)" package="0603 [SMD]"]
  Slider_3_Green_LED = LED - 5mm [color="Green (560nm)" current=0.030 package="5 mm [THT]"]
  R4 = Resistor [tolerance=±5% power=0.25 resistance=220 package=THT]
  R5 = Resistor [tolerance=±5% power=0.25 resistance=220 package=THT]
  R6 = Resistor [tolerance=±5% power=0.25 resistance=220 package=THT]
  Command_and_Power = JST-03JQ-BT [part_number=JST-JQ-BT package=THT]
  Volt_Meter = meter

nets:
  GND: Part1.GND, Slider_1.leg1, Slider_2.leg1, Slider_3.leg1, Part3.GND, Slider_1_Green_LED.cathode, Slider_2_Red_LED.cathode, Slider_3_Green_LED.cathode, Command_and_Power.pin3
  N1: Part1.D2, R6.Pin_0
  N2: Part1.D3, R5.Pin_0
  N3: Part1.D4, R4.Pin_0
  N4: Part1.D9, Volt_Meter.Positive
  N5: Part1.D10, Volt_Meter.Com
  VIN: Part1.VIN, Part3.VDD, Command_and_Power.pin2
  N6: Part1.A4, Slider_1.wiper
  N7: Part1.A3, Slider_2.wiper
  N8: Part1.A2, Slider_3.wiper
  N9: Part1.A1, Command_and_Power.pin1
  N10: Part1.A0, Part3.IN
  N11: Part1.AREF, Slider_1.leg2, Slider_2.leg2, Slider_3.leg2
  N12: Slider_1_Green_LED.anode, R4.Pin_1
  N13: Slider_2_Red_LED.anode, R5.Pin_1
  N14: Slider_3_Green_LED.anode, R6.Pin_1

custom parts:
  Adafruit Breadboard-Friendly NeoPixel: This is the easiest way possible to add small, bright RGB pixels to your project. We took the same technology from our Flora NeoPixels and made them breadboard friendly, with two rows of 3 x 0.1" spaced header on each side for easy soldering, chaining and breadboarding. These ultra-bright LEDs have a constant-current driver cooked right into the LED package! The pixels are chainable - so you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
  meter: A generic analog meter.
