# Fritzing sketch Controller Breadboard Schematic (saved by Fritzing 0.9.10b)
breadboards: 1

parts:
  Part1 = Arduino Nano (Rev3.0)
  Status_LED = Adafruit Breadboard-Friendly NeoPixel [part_number="Adafruit #1312"]
  SP1 = SPEAKER [package=pcb_mount_speaker]
  R1 = Resistor [tolerance=±5% power=0.25 resistance=1k package=THT]
  R2 = Resistor [tolerance=±5% power=0.25 resistance=2k package=THT]
  Command_and_Power = JST-03JQ-BT [part_number=JST-JQ-BT package=THT]
  20x4_Char_LCD = LCD2004-I2C
  R3 = Resistor [tolerance=±5% power=0.25 resistance=2k package=THT]
  R4 = Resistor [tolerance=±5% power=0.25 resistance=1k package=THT]
  R5 = Resistor [tolerance=±5% power=0.25 resistance=2k package=THT]
  R6 = Resistor [tolerance=±5% power=0.25 resistance=1k package=THT]
  R7 = Resistor [tolerance=±5% power=0.25 resistance=2k package=THT]
  R8 = Resistor [tolerance=±5% power=0.25 resistance=1k package=THT]
  R9 = Resistor [tolerance=±5% power=0.25 resistance=2k package=THT]
  R10 = Resistor [tolerance=±5% power=0.25 resistance=1k package=THT]
  R11 = Resistor [tolerance=±5% power=0.25 resistance=2k package=THT]
  R12 = Resistor [tolerance=±5% power=0.25 resistance=1k package=THT]
  LOLIN_2_4_TFT = 2.4 Touchscreen TFT Breakout w:MicroSD

nets:
  GND: Part1.GND, Status_LED.GND, SP1.+, R2.Pin_0, Command_and_Power.pin3, 20x4_Char_LCD.GND, R3.Pin_0, R5.Pin_0, R7.Pin_0, R9.Pin_0, R11.Pin_0, LOLIN_2_4_TFT.GND
  N1: Part1.D4, SP1.-
  N2: Part1.D7, R12.Pin_1
  N3: Part1.D8, R10.Pin_1
  N4: Part1.D9, R8.Pin_1
  N5: Part1.D10, R6.Pin_1
  N6: Part1.D11/MOSI, R4.Pin_1
  N7: Part1.D12/MISO, LOLIN_2_4_TFT.MISO
  VIN: Part1.VIN, Status_LED.VDD, Command_and_Power.pin2, 20x4_Char_LCD.VCC
  N8: Part1.A5, 20x4_Char_LCD.SCL
  N9: Part1.A4, 20x4_Char_LCD.SDA
  N10: Part1.A1, Command_and_Power.pin1
  N11: Part1.A0, Status_LED.IN
  3V3: Part1.3V3, LOLIN_2_4_TFT.VIN
  N12: Part1.D13/SCK, R1.Pin_1
  N13: R1.Pin_0, R2.Pin_1, LOLIN_2_4_TFT.CLK
  N14: R3.Pin_1, R4.Pin_0, LOLIN_2_4_TFT.MOSI
  N15: R5.Pin_1, R6.Pin_0, LOLIN_2_4_TFT.WR_DC
  N16: R7.Pin_1, R8.Pin_0, LOLIN_2_4_TFT.CS
  N17: R9.Pin_1, R10.Pin_0, LOLIN_2_4_TFT.RST
  N18: R11.Pin_1, R12.Pin_0, LOLIN_2_4_TFT.SD_CS

notes:
  Wiring for 2.4 TFT is not exact. I could not find a matching Fritzing part.

custom parts:
  Adafruit Breadboard-Friendly NeoPixel: This is the easiest way possible to add small, bright RGB pixels to your project. We took the same technology from our Flora NeoPixels and made them breadboard friendly, with two rows of 3 x 0.1" spaced header on each side for easy soldering, chaining and breadboarding. These ultra-bright LEDs have a constant-current driver cooked right into the LED package! The pixels are chainable - so you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
  LCD2004-I2C: A standard character display with 4x20 characters. Comes in many colors with LCM2004 IIC attached.
  2.4 Touchscreen TFT Breakout w:MicroSD: Add some jazz & pizzazz to your project with a color touchscreen LCD. This TFT display is 2.4" diagonal with a bright (4 white-LED) backlight and it's colorful! 240x320 pixels with individual RGB pixel control, this has way more resolution than a black and white 128x64 display. As a bonus, this display has a resistive touchscreen attached to it already, so you can detect finger presses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
