# Fritzing sketch FlipBits Breadboard Schematic (saved by Fritzing 0.9.10b)
breadboards: 1

parts:
  Part1 = Arduino Nano (Rev3.0)
  Status_LED = Adafruit Breadboard-Friendly NeoPixel [part_number="Adafruit #1312"]
  Command_and_Power = JST-03JQ-BT [part_number=JST-JQ-BT package=THT]
  S2^7 = Taiway 100-SP-X-T1 SPDT Miniature Toggle Switch [package=THT]
  S2^6 = Taiway 100-SP-X-T1 SPDT Miniature Toggle Switch [package=THT]
  S2^5 = Taiway 100-SP-X-T1 SPDT Miniature Toggle Switch [package=THT]
  S2^4 = Taiway 100-SP-X-T1 SPDT Miniature Toggle Switch [package=THT]
  S2^3 = Taiway 100-SP-X-T1 SPDT Miniature Toggle Switch [package=THT]
  S2^2 = Taiway 100-SP-X-T1 SPDT Miniature Toggle Switch [package=THT]
  S2^1 = Taiway 100-SP-X-T1 SPDT Miniature Toggle Switch [package=THT]
  S2^0 = Taiway 100-SP-X-T1 SPDT Miniature Toggle Switch [package=THT]
  High_Nibble = 7-Segment LED Display [package=THT]
  U1 = MCP23017 [package="DIP (Dual Inline) [THT]"]
  Low_Nibble = 7-Segment LED Display [package=THT]
  R1 = Resistor [tolerance=±5% resistance=220 package="0603 [SMD]"]
  R2 = Resistor [tolerance=±5% resistance=220 package="0603 [SMD]"]
  R3 = Resistor [tolerance=±5% resistance=220 package="0603 [SMD]"]
  R4 = Resistor [tolerance=±5% resistance=220 package="0603 [SMD]"]
  R5 = Resistor [tolerance=±5% resistance=220 package="0603 [SMD]"]
  R6 = Resistor [tolerance=±5% resistance=220 package="0603 [SMD]"]
  R7 = Resistor [tolerance=±5% resistance=220 package="0603 [SMD]"]
  R8 = Resistor [tolerance=±5% resistance=220 package="0603 [SMD]"]
  R9 = Resistor [tolerance=±5% resistance=220 package="0603 [SMD]"]
  R10 = Resistor [tolerance=±5% resistance=220 package="0603 [SMD]"]
  R11 = Resistor [tolerance=±5% resistance=220 package="0603 [SMD]"]
  R12 = Resistor [tolerance=±5% resistance=220 package="0603 [SMD]"]
  R13 = Resistor [tolerance=±5% resistance=220 package="0603 [SMD]"]
  R14 = Resistor [tolerance=±5% resistance=220 package="0603 [SMD]"]
  R15 = Resistor [tolerance=±5% resistance=220 package="0603 [SMD]"]
  R16 = Resistor [tolerance=±5% resistance=220 package="0603 [SMD]"]

nets:
  GND: Part1.GND, Status_LED.GND, Command_and_Power.pin3, S2^7.COM, S2^6.COM, S2^5.COM, S2^4.COM, S2^3.COM, S2^2.COM, S2^1.COM, S2^0.COM, U1.GND, U1.A0, U1.A1, U1.A2
  N1: Part1.D2, S2^7.L1
  N2: Part1.D3, S2^6.L1
  N3: Part1.D4, S2^5.L1
  N4: Part1.D5, S2^4.L1
  N5: Part1.D6, S2^3.L1
  N6: Part1.D7, S2^2.L1
  N7: Part1.D8, S2^1.L1
  N8: Part1.D9, S2^0.L1
  VIN: Part1.VIN, Status_LED.VDD, Command_and_Power.pin2, High_Nibble.commAnode, U1.VCC, U1.RST, Low_Nibble.commAnode
  N9: Part1.A5, U1.SCL
  N10: Part1.A4, U1.SDA
  N11: Part1.A1, Command_and_Power.pin1
  N12: Part1.A0, Status_LED.IN
  N13: High_Nibble.cathodeE, R1.Pin_0
  N14: High_Nibble.cathodeD, R2.Pin_0
  N15: High_Nibble.cathodeC, R3.Pin_0
  N16: High_Nibble.cathodeDP, R4.Pin_0
  N17: High_Nibble.cathodeB, R12.Pin_1
  N18: High_Nibble.cathodeA, R11.Pin_1
  N19: High_Nibble.cathodeF, R10.Pin_1
  N20: High_Nibble.cathodeG, R9.Pin_1
  N21: U1.GPB0, R11.Pin_0
  N22: U1.GPB1, R12.Pin_0
  N23: U1.GPB2, R3.Pin_1
  N24: U1.GPB3, R2.Pin_1
  N25: U1.GPB4, R1.Pin_1
  N26: U1.GPB5, R10.Pin_0
  N27: U1.GPB6, R9.Pin_0
  N28: U1.GPB7, R4.Pin_1
  N29: U1.GPA0, R15.Pin_0
  N30: U1.GPA1, R16.Pin_0
  N31: U1.GPA2, R7.Pin_1
  N32: U1.GPA3, R6.Pin_1
  N33: U1.GPA4, R5.Pin_1
  N34: U1.GPA5, R14.Pin_0
  N35: U1.GPA6, R13.Pin_0
  N36: U1.GPA7, R8.Pin_1
  N37: Low_Nibble.cathodeE, R5.Pin_0
  N38: Low_Nibble.cathodeD, R6.Pin_0
  N39: Low_Nibble.cathodeC, R7.Pin_0
  N40: Low_Nibble.cathodeDP, R8.Pin_0
  N41: Low_Nibble.cathodeB, R16.Pin_1
  N42: Low_Nibble.cathodeA, R15.Pin_1
  N43: Low_Nibble.cathodeF, R14.Pin_1
  N44: Low_Nibble.cathodeG, R13.Pin_1

notes:
  Upper Nibble
  Lower Nibble

custom parts:
  Adafruit Breadboard-Friendly NeoPixel: This is the easiest way possible to add small, bright RGB pixels to your project. We took the same technology from our Flora NeoPixels and made them breadboard friendly, with two rows of 3 x 0.1" spaced header on each side for easy soldering, chaining and breadboarding. These ultra-bright LEDs have a constant-current driver cooked right into the LED package! The pixels are chainable - so you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
  MCP23017: 16 bit I/O chip controlled via I2C
