# Fritzing sketch Power Breadboard Schematic (saved by Fritzing 0.9.10b)
breadboards: 1

parts:
  U1 = 555 Timer [package="DIP8 [THT]"]
  LED = smd LED [color="Red (633nm)" package="0603 [SMD]"]
  R1 = Resistor [tolerance=±5% power=0.25 resistance=220 package=THT]
  Part1 = Adafruit Micro USB Breakout [part_number="Adafruit #1833"]
  Power = JST-03JQ-BT [part_number=JST-JQ-BT package=THT]
  BUTTON1 = Waterproof Pushbutton (green)
  R2 = Resistor [tolerance=±5% power=0.25 resistance=220 package=THT]
  R3 = Resistor [tolerance=±5% power=0.25 resistance=1k package=THT]
  C1 = Electrolytic Capacitor [capacitance=10µF voltage=35V package="100 mil [THT, electrolytic]"]
  R4 = Resistor [tolerance=±5% power=0.25 resistance=100k package=THT]

nets:
  N1: U1.Ground, Part1.GND, Power.pin3, BUTTON1.no_name_yet#5, R2.Pin_1, C1.-
  N2: U1.Trigger, U1.Threshold, C1.+, R4.Pin_0
  N3: U1.Output, LED.anode
  N4: U1.Reset, U1.Vcc_Supply_Voltage, R1.Pin_1, Power.pin2, BUTTON1.no_name_yet#2, R3.Pin_1
  N5: U1.Discharge, R3.Pin_0, R4.Pin_1
  N6: LED.cathode, R2.Pin_0
  N7: R1.Pin_0, BUTTON1.no_name_yet#4
  N8: Part1.VBUS, BUTTON1.no_name_yet#1

custom parts:
  Adafruit Micro USB Breakout: Simple but effective - this breakout board has a USB Micro-B connector, with all 5 pins broken out. Great for pairing with a microcontroller with USB support, or adding USB 5V power to a project. We use a micro-AB connector with through-hole shielding pads for an excellent strong connection - it won't rip off by accident! Comes with one fully assembled and tested micro B breakout PCB and a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
  Waterproof Pushbutton (green): Waterproof Illuminated Pushbutton (green)
