# Fritzing sketch SpinDigit Breadboard Schematic (saved by Fritzing 0.9.10b)
breadboards: 2

parts:
  Part1 = Arduino Nano (Rev3.0)
  Status_LED = Adafruit Breadboard-Friendly NeoPixel [part_number="Adafruit #1312"]
  Command_and_Power = JST-03JQ-BT [part_number=JST-JQ-BT package=THT]
  10_Digit_Rotary_Dial_1 = Hexadecimal Rotary Encoder [package=THT]
  10_Digit_Rotary_Dial_2 = Hexadecimal Rotary Encoder [package=THT]
  10_Digit_Rotary_Dial_3 = Hexadecimal Rotary Encoder [package=THT]
  IC1 = LM3914 [chip_label=LM3914 package="DIP (Dual Inline) [THT]"]
  LED_Bar_1 = LED_BARGRAPH_10 [package=led_bargaph_10]
  IC2 = LM3914 [chip_label=LM3914 package="DIP (Dual Inline) [THT]"]
  LED_Bar_2 = LED_BARGRAPH_10 [package=led_bargaph_10]
  IC3 = MCP23017 I2C I/O Expander
  R1 = Resistor [tolerance=±5% resistance=1.2k package="2512 [SMD]"]
  R2 = Resistor [tolerance=±5% resistance=1.1k package="2512 [SMD]"]
  R3 = Resistor [tolerance=±5% resistance=2.4k package="2512 [SMD]"]
  R4 = Resistor [tolerance=±5% resistance=2.4k package="2512 [SMD]"]
  R5 = Resistor [tolerance=±5% resistance=12k package="2512 [SMD]"]
  C5 = Electrolytic Capacitor [capacitance=4.7µF voltage=35V package="0405 [SMD, electrolytic]"]
  R6 = Resistor [tolerance=±5% resistance=12k package="2512 [SMD]"]
  C6 = Electrolytic Capacitor [capacitance=4.7µF voltage=35V package="0405 [SMD, electrolytic]"]
  Light_3 = LED Sequin - Warm White
  Light_2 = LED Sequin - Warm White
  Light_1 = LED Sequin - Warm White

nets:
  GND: Part1.GND, Status_LED.GND, Command_and_Power.pin3, 10_Digit_Rotary_Dial_1.InputCommon, 10_Digit_Rotary_Dial_1.InputCommon2, 10_Digit_Rotary_Dial_2.InputCommon, 10_Digit_Rotary_Dial_2.InputCommon2, 10_Digit_Rotary_Dial_3.InputCommon, 10_Digit_Rotary_Dial_3.InputCommon2, IC1.pin2, IC1.pin4, IC2.pin2, IC2.pin4, IC3.VSS, IC3.A0, IC3.A1, IC3.A2, R3.Pin_0, R4.Pin_0, C5.-, C6.-, Light_3.-, Light_2.-, Light_1.-
  N1: Part1.D2, Light_3.+, Light_2.+, Light_1.+
  N2: Part1.D5, R5.Pin_1
  N3: Part1.D6, R6.Pin_1
  VDD: Part1.VIN, Status_LED.VDD, Command_and_Power.pin2, IC1.pin3, IC1.pin9, LED_Bar_1.A_A, LED_Bar_1.B_A, LED_Bar_1.C_A, LED_Bar_1.D_A, LED_Bar_1.E_A, LED_Bar_1.F_A, LED_Bar_1.G_A, LED_Bar_1.H_A, LED_Bar_1.I_A, LED_Bar_1.J_A, IC2.pin3, IC2.pin9, LED_Bar_2.A_A, LED_Bar_2.B_A, LED_Bar_2.C_A, LED_Bar_2.D_A, LED_Bar_2.E_A, LED_Bar_2.F_A, LED_Bar_2.G_A, LED_Bar_2.H_A, LED_Bar_2.I_A, LED_Bar_2.J_A, IC3.VDD, IC3.RESET
  N4: Part1.A5, IC3.SCL
  N5: Part1.A4, IC3.SDA
  N6: Part1.A1, Command_and_Power.pin1
  N7: Part1.A0, Status_LED.IN
  N8: 10_Digit_Rotary_Dial_1.Output1Pin, IC3.GPA0
  N9: 10_Digit_Rotary_Dial_1.Output2Pin, IC3.GPA1
  N10: 10_Digit_Rotary_Dial_1.Output4Pin, IC3.GPA2
  N11: 10_Digit_Rotary_Dial_1.Output8pin, IC3.GPA3
  N12: 10_Digit_Rotary_Dial_2.Output1Pin, IC3.GPA4
  N13: 10_Digit_Rotary_Dial_2.Output2Pin, IC3.GPA5
  N14: 10_Digit_Rotary_Dial_2.Output4Pin, IC3.GPA6
  N15: 10_Digit_Rotary_Dial_2.Output8pin, IC3.GPA7
  N16: 10_Digit_Rotary_Dial_3.Output1Pin, IC3.GPB0
  N17: 10_Digit_Rotary_Dial_3.Output2Pin, IC3.GPB1
  N18: 10_Digit_Rotary_Dial_3.Output4Pin, IC3.GPB2
  N19: 10_Digit_Rotary_Dial_3.Output8pin, IC3.GPB3
  N20: IC1.pin1, LED_Bar_1.A_C
  N21: IC1.pin5, R6.Pin_0, C6.+
  N22: IC1.pin6, IC1.pin7, R1.Pin_0, R4.Pin_1
  N23: IC1.pin8, R1.Pin_1
  N24: IC1.pin10, LED_Bar_1.J_C
  N25: IC1.pin11, LED_Bar_1.I_C
  N26: IC1.pin12, LED_Bar_1.H_C
  N27: IC1.pin13, LED_Bar_1.G_C
  N28: IC1.pin14, LED_Bar_1.F_C
  N29: IC1.pin15, LED_Bar_1.E_C
  N30: IC1.pin16, LED_Bar_1.D_C
  N31: IC1.pin17, LED_Bar_1.C_C
  N32: IC1.pin18, LED_Bar_1.B_C
  N33: IC2.pin1, LED_Bar_2.A_C
  N34: IC2.pin5, R5.Pin_0, C5.+
  N35: IC2.pin6, IC2.pin7, R2.Pin_0, R3.Pin_1
  N36: IC2.pin8, R2.Pin_1
  N37: IC2.pin10, LED_Bar_2.J_C
  N38: IC2.pin11, LED_Bar_2.I_C
  N39: IC2.pin12, LED_Bar_2.H_C
  N40: IC2.pin13, LED_Bar_2.G_C
  N41: IC2.pin14, LED_Bar_2.F_C
  N42: IC2.pin15, LED_Bar_2.E_C
  N43: IC2.pin16, LED_Bar_2.D_C
  N44: IC2.pin17, LED_Bar_2.C_C
  N45: IC2.pin18, LED_Bar_2.B_C

custom parts:
  Adafruit Breadboard-Friendly NeoPixel: This is the easiest way possible to add small, bright RGB pixels to your project. We took the same technology from our Flora NeoPixels and made them breadboard friendly, with two rows of 3 x 0.1" spaced header on each side for easy soldering, chaining and breadboarding. These ultra-bright LEDs have a constant-current driver cooked right into the LED package! The pixels are chainable - so you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
  LM3914: LM3914 Dot/Bar Display Driver
  MCP23017 I2C I/O Expander: The MCP23017 uses two i2c pins (these can be shared with other i2c devices), and in exchange gives you 16 general purpose pins. You can set each of 16 pins to be input, output, input with a pullup or open drain. There's even the ability to get an interrupt via an external pin when any of the inputs change so you don't have to keep polling the chip.
  LED Sequin - Warm White: Sew a little sparkle into your wearable project with an Adafruit LED Sequin. Simply connect 3 to 6VDC to the + pin and ground to the - pin, and the LED on the board will light up. You can make the LEDs fade and twinkle by using PWM.
